// Logisim project oblig1.circ as structural Verilog: 3 circuits, main circuit Kombinatorisk krets
module Kombinatorisk_krets (
  input  A0,
  input  A1,
  input  A2,
  input  A3,
  output f0,
  output f1,
  output f2,
  output f3,
  output f4,
  output f5,
  output f6,
  output f7
);

  wire fulladder_1_out_5, halvadder_1_c, halvadder_2_c;

  Halvadder halvadder_1 (.in_1(A0), .in_2(A2), .S(f4), .C(halvadder_1_c));
  Fulladder fulladder_1 (.in_2(A1), .in_3(A3), .Menteinn(halvadder_1_c), .out_4(f3), .out_5(fulladder_1_out_5));
  Halvadder halvadder_2 (.in_1(fulladder_1_out_5), .in_2(A2), .S(f2), .C(halvadder_2_c));
  Halvadder halvadder_3 (.in_1(halvadder_2_c), .in_2(A3), .S(f1), .C(f0));

  assign f5 = A1;
  assign f6 = A0;
  assign f7 = 1'b0;
endmodule

// Halv
module Halvadder (
  input  in_1,
  input  in_2,
  output S,
  output C
);

  xor xor_1 (S, in_1, in_2);
  and and_1 (C, in_1, in_2);
endmodule

// Full
module Fulladder (
  input  Menteinn,
  input  in_2,
  input  in_3,
  output out_4,
  output out_5
);

  wire and_1_out, and_2_out, xor_1_out;

  and and_1 (and_1_out, in_2, in_3);
  xor xor_1 (xor_1_out, in_2, in_3);
  xor xor_2 (out_4, xor_1_out, Menteinn);
  and and_2 (and_2_out, xor_1_out, Menteinn);
  or or_1 (out_5, and_2_out, and_1_out);
endmodule
