// Logisim project oblig1.circ as structural Verilog: 3 circuits, main circuit main
module main (
  input  A3,
  input  A2,
  input  A1,
  input  A0,
  output out_5,
  output out_6,
  output out_7,
  output out_8,
  output out_9,
  output out_10,
  output out_11,
  output out_12
);

  wire fullladder_1_out_4, halvadder_1_out_3, halvadder_2_out_3;

  Halvadder halvadder_1 (.in_1(A2), .in_2(A0), .out_3(halvadder_1_out_3), .out_4(out_9));
  Fullladder fullladder_1 (.in_1(A3), .in_2(A1), .in_3(halvadder_1_out_3), .out_4(fullladder_1_out_4), .out_5(out_8));
  Halvadder halvadder_2 (.in_1(A2), .in_2(fullladder_1_out_4), .out_3(halvadder_2_out_3), .out_4(out_7));
  Halvadder halvadder_3 (.in_1(A3), .in_2(halvadder_2_out_3), .out_3(out_5), .out_4(out_6));

  assign out_10 = A1;
  assign out_11 = A0;
  assign out_12 = 1'b0;
endmodule

module Halvadder (
  input  in_1,
  input  in_2,
  output out_3,
  output out_4
);

  and and_1 (out_3, in_1, in_2);
  xor xor_1 (out_4, in_1, in_2);
endmodule

module Fullladder (
  input  in_1,
  input  in_2,
  input  in_3,
  output out_4,
  output out_5
);

  wire and_1_out, and_2_out, xor_1_out;

  and and_1 (and_1_out, in_1, in_2);
  xor xor_1 (xor_1_out, in_1, in_2);
  and and_2 (and_2_out, xor_1_out, in_3);
  xor xor_2 (out_5, xor_1_out, in_3);
  or or_1 (out_4, and_1_out, and_2_out);
endmodule
