// Logisim project Oblig 1.circ as structural Verilog: 9 circuits, main circuit main
module main (
  input  a3,
  input  a2,
  input  a1,
  input  a0,
  output out_5,
  output out_6,
  output out_7,
  output out_8,
  output out_9,
  output out_10,
  output out_11,
  output out_12
);

  b7 b7 (.a3(a3), .a2(a2), .a1(a1), .a0(a0), .b7(out_5));
  b6 b6 (.a3(a3), .a2(a2), .a1(a1), .a0(a0), .b6(out_6));
  b5 b5 (.a3(a3), .a2(a2), .a1(a1), .a0(a0), .b5(out_7));
  b4 b4 (.a3(a3), .a2(a2), .a1(a1), .a0(a0), .b4(out_8));
  b3 b3 (.a3(a3), .a2(a2), .a1(a1), .a0(a0), .out_5(out_9));
  b2 b2 (.a3(a3), .a2(a2), .a1(a1), .a0(a0), .b2(out_10));
  b1 b1 (.a3(a3), .a2(a2), .a1(a1), .a0(a0), .b1(out_11));
  b0 b0 (.a(a3), .b(a2), .c(a1), .d(a0), .x(out_12));

  // Notes on the sheet:
  //   Les nedover
  //   Les nedover
endmodule

module b7 (
  input  a3,
  input  a2,
  input  a1,
  input  a0,
  output b7
);

  wire and_1_out, and_2_out;

  and and_1 (and_1_out, a3, a2, a0);
  and and_2 (and_2_out, a3, a2, a1);
  or or_1 (b7, and_1_out, and_2_out);

  // Notes on the sheet:
  //   Krets til b7
  //   b7 = abd+abc
endmodule

module b6 (
  input  a3,
  input  a2,
  input  a1,
  input  a0,
  output b6
);

  wire and_1_out, and_2_out, and_3_out, not_1_out, not_2_out, not_3_out, not_4_out;

  not not_1 (not_1_out, a3);
  and and_1 (and_1_out, not_1_out, a2, a1, a0);
  not not_2 (not_2_out, a2);
  and and_2 (and_2_out, not_2_out, a3);
  not not_3 (not_3_out, a1);
  and and_3 (and_3_out, a3, not_3_out, not_4_out);
  not not_4 (not_4_out, a0);
  or or_1 (b6, and_1_out, and_2_out, and_3_out);

  // Notes on the sheet:
  //   Krets til b6
  //   b6 = a´bcd+ab´+ac´d´
endmodule

module b5 (
  input  a3,
  input  a2,
  input  a1,
  input  a0,
  output b5
);

  wire and_1_out, and_2_out, and_3_out, and_4_out, not_1_out, not_2_out, not_3_out, not_4_out;

  not not_1 (not_1_out, a3);
  not not_2 (not_2_out, a2);
  not not_3 (not_3_out, a1);
  not not_4 (not_4_out, a0);
  and and_1 (and_1_out, not_1_out, a2, not_3_out);
  and and_2 (and_2_out, not_1_out, a2, not_4_out);
  and and_3 (and_3_out, a2, not_3_out, not_4_out);
  and and_4 (and_4_out, a3, not_2_out, a1);
  or or_1 (b5, and_1_out, and_2_out, and_3_out, and_4_out);

  // Notes on the sheet:
  //   Krets til b5
  //   b5 = a´bc´+a´bd´+bc´d´+ab´c
endmodule

module b4 (
  input  a3,
  input  a2,
  input  a1,
  input  a0,
  output b4
);

  wire and_1_out, and_2_out, and_3_out, and_4_out, and_5_out, and_6_out, not_1_out, not_2_out, not_3_out,
       not_4_out;

  not not_1 (not_1_out, a3);
  not not_2 (not_2_out, a2);
  not not_3 (not_3_out, a1);
  not not_4 (not_4_out, a0);
  and and_1 (and_1_out, not_1_out, not_2_out, a1);
  and and_2 (and_2_out, not_1_out, a1, not_4_out);
  and and_3 (and_3_out, a3, not_2_out, not_3_out);
  and and_4 (and_4_out, a3, not_3_out, not_4_out);
  and and_5 (and_5_out, not_1_out, a2, not_3_out, a0);
  and and_6 (and_6_out, a3, a2, a1, a0);
  or or_1 (b4, and_1_out, and_2_out, and_3_out, and_4_out, and_5_out, and_6_out);

  // Notes on the sheet:
  //   Kretsen til b4
  //   b4 = a´b´c+a´bd´+ab´c´+ac´d´+a´bc´d+abcd
endmodule

module b3 (
  input  a3,
  input  a2,
  input  a1,
  input  a0,
  output out_5
);

  xor xor_1 (out_5, a2, a0);

  // Notes on the sheet:
  //   Krets for b3
  //   b3 = bd´+b´d
endmodule

module b2 (
  input  a3,
  input  a2,
  input  a1,
  input  a0,
  output b2
);


  assign b2 = a1;

  // Notes on the sheet:
  //   Krets for b2
  //   b2 = c
endmodule

module b1 (
  input  a3,
  input  a2,
  input  a1,
  input  a0,
  output b1
);


  assign b1 = a0;

  // Notes on the sheet:
  //   Krets for b1
  //   b1 = d
endmodule

module b0 (
  input  a,
  input  b,
  input  c,
  input  d,
  output x
);


  assign x = 1'b0;

  // Notes on the sheet:
  //   Krets for b0
  //   b0 = 0
endmodule
