// Logisim project oblig1.circ as structural Verilog: 1 circuit, main circuit oblig1
module oblig1 (
  input  x2,
  input  x1,
  input  x0,
  output a,
  output b,
  output c,
  output d,
  output e,
  output f,
  output g
);

  wire and_2_out, and_3_out, and_4_out, and_5_out, and_6_out, and_7_out, and_8_out, and_9_out, and_out,
       not_1_out, not_2_out, not_3_out, not_4_out, not_5_out, not_6_out, not_7_out, not_8_out, not_9_out,
       not_10_out, not_11_out, not_12_out, not_13_out, not_14_out;

  not not_1 (not_1_out, x2);
  not not_2 (not_2_out, x0);
  not not_3 (not_3_out, x2);
  not not_4 (not_4_out, x1);
  not not_5 (not_5_out, x0);
  not not_6 (not_6_out, x1);
  not not_7 (not_7_out, x2);
  not not_8 (not_8_out, x0);
  not not_9 (not_9_out, x2);
  not not_10 (not_10_out, x0);
  not not_11 (not_11_out, x0);
  not not_12 (not_12_out, x1);
  not not_13 (not_13_out, x0);
  or \or  (g, x1, x2);
  and \and  (and_out, not_1_out, not_2_out);
  or or_2 (a, and_out, and_2_out, and_3_out);
  and and_2 (and_2_out, not_3_out, x1);
  and and_3 (and_3_out, x2, x0);
  not not_14 (not_14_out, x2);
  or or_3 (b, not_14_out, and_4_out);
  and and_4 (and_4_out, not_4_out, not_5_out);
  or or_4 (c, not_6_out, x0, x2);
  and and_5 (and_5_out, not_7_out, not_8_out);
  or or_5 (d, and_5_out, x1, and_6_out);
  and and_6 (and_6_out, x2, x0);
  and and_7 (and_7_out, not_9_out, not_10_out);
  or or_6 (e, and_7_out, and_8_out);
  and and_8 (and_8_out, x1, not_11_out);
  and and_9 (and_9_out, not_12_out, not_13_out);
  or or_7 (f, and_9_out, x2);
  _7_Segment_Display u_7_segment_display_1 (.g(g), .f(f), .a(a), .b(b), .e(e), .d(d), .c(c));  // open: dp

  // Notes on the sheet:
  //   sarime
  //   INF 1400
  //   oblig1
  //   3 Bits input
  //   Binær til 7 segments decoder
  //   7 Bits output
endmodule
